# Fritzing sketch Arduino_4LED_newv2 (saved by Fritzing 0.9.2b)
breadboards: 1

parts:
  Part1 = Arduino Motor Shield
  Part3 = Arduino Uno (Rev3)  # not connected
  LED1 = LED - 5mm [color="Red (633nm)" package="5 mm [THT]"]
  R1 = Resistor [tolerance=±5% resistance=220 package=THT]
  LED3 = LED - 5mm [color="Blue (525nm)" package="5 mm [THT]"]
  LED4 = LED - 5mm [color="Yellow (595nm)" package="5 mm [THT]"]
  LED2 = smd LED [color="Green (570nm)" package="1206 [SMD]"]
  R3 = Resistor [tolerance=±5% resistance=220 package=THT]
  R4 = Resistor [tolerance=±5% resistance=220 package=THT]
  R5 = Resistor [tolerance=±5% resistance=220 package=THT]

nets:
  N1: Part1.D4, R4.Pin_0
  N2: Part1.D5, R5.Pin_0
  N3: Part1.D6, R3.Pin_0
  N4: Part1.D7, R1.Pin_0
  N5: Part1.GND, LED1.cathode, LED3.cathode, LED4.cathode, LED2.cathode
  N6: LED1.anode, R3.Pin_1
  N7: R1.Pin_1, LED3.anode
  N8: LED4.anode, R5.Pin_1
  N9: LED2.anode, R4.Pin_1
