# Fritzing sketch Arduino_IR_Compass_4LED_newv2 (saved by Fritzing 0.9.2b)
breadboards: 1

parts:
  Part1 = Arduino Motor Shield
  Part2 = Triple Axis Magnetometer - HMC5883 Breakout
  Part3 = Arduino Uno (Rev3)  # not connected
  LED1 = LED - 5mm [color="Red (633nm)" package="5 mm [THT]"]
  R1 = Resistor [tolerance=±5% resistance=220 package=THT]
  LED3 = LED - 5mm [color="Blue (525nm)" package="5 mm [THT]"]
  LED4 = LED - 5mm [color="Yellow (595nm)" package="5 mm [THT]"]
  LED2 = smd LED [color="Green (570nm)" package="1206 [SMD]"]
  R3 = Resistor [tolerance=±5% resistance=220 package=THT]
  R4 = Resistor [tolerance=±5% resistance=220 package=THT]
  R5 = Resistor [tolerance=±5% resistance=220 package=THT]
  J1 = Infrared Proximity Sensor

nets:
  3.3V: Part1.3.3V, Part2.VCC
  5V: Part1.5V, J1.Vcc
  N1: Part1.A4, Part2.SDA
  N2: Part1.A5, Part2.SCL
  N3: Part1.D4, R4.Pin_0
  N4: Part1.D5, R5.Pin_0
  N5: Part1.D6, R3.Pin_0
  N6: Part1.D7, R1.Pin_0
  GND: Part1.D8, Part1.GND, LED1.cathode, LED3.cathode, LED4.cathode, LED2.cathode, J1.GND
  N7: LED1.anode, R3.Pin_1
  N8: R1.Pin_1, LED3.anode
  N9: LED4.anode, R5.Pin_1
  N10: LED2.anode, R4.Pin_1

notes:
  Wire will enable robot to move:
  5V->Move
  Gnd->Stop
